# Fritzing sketch PCBBarometricSensor (saved by Fritzing 0.9.3b)
circuit board: 8.46667cm x 5.64444cm
breadboards: 1

parts:
  JP1 = Header 12 [package=1x12_machine-pin-header_lock.004]
  Raspberry_Pi_1 = Raspberry Pi 3 [part_number=RPI-3-V1.2]

nets (from the pcb view):
  N1: JP1.1, Raspberry_Pi_1.3v3
  N2: JP1.2, JP1.6, Raspberry_Pi_1.GND
  N3: JP1.3, Raspberry_Pi_1.GPIO3
  N4: JP1.4, Raspberry_Pi_1.GPIO2
